# Fritzing sketch http2copper-wire-lights (saved by Fritzing 0.9.3b)
breadboards: 1

parts:
  WeMos_D1_Mini1 = WeMos D1 Mini  # not connected
  IC1 = L293D [package=THT]

nets:
  N1: IC1.Enable_1, IC1.+Vmotor
